// Logisim project alu.circ as structural Verilog: 2 circuits, main circuit alu
module alu (
  input  [31:0] A,
  input  [31:0] B,
  input  [3:0] ALUSel,
  output [31:0] Result
);

  wire comparator_1_lt;
  wire [31:0] add0, and1, divu8, mul10, mulh14, mulhu11, or2, remu9, sll6, slt7, sra5, srl4, sub12, xor3;

  Adder #(.width(32)) adder_1 (.a(A), .b(B), .out(add0));  // open: cin, cout
  assign and1 = A & B;  // AND_Gate and_1, 32 bits wide
  assign or2 = A | B;  // OR_Gate or_1, 32 bits wide
  assign xor3 = A ^ B;  // XOR_Gate xor_1, 32 bits wide
  Shifter #(.width(32), .shift("lr")) shifter_1 (.in(A), .\dist (B[4:0]), .out(srl4));
  Shifter #(.width(32), .shift("ar")) shifter_2 (.in(A), .\dist (B[4:0]), .out(sra5));
  Shifter #(.width(32)) shifter_3 (.in(A), .\dist (B[4:0]), .out(sll6));
  Comparator #(.width(32)) comparator_1 (.a(A), .b(B), .lt(comparator_1_lt));  // open: gt, eq
  Divider #(.width(32)) divider_1 (.a(A), .b(B), .out(divu8), .rem(remu9));  // open: upper
  Subtractor #(.width(32)) subtractor_1 (.a(A), .b(B), .out(sub12));  // open: bin, bout
  assign slt7 = {{31{1'b0}}, comparator_1_lt};  // Bit_Extender bit_extender_1
  mul_helper mul_helper_1 (.input_1(A), .input_2(B), .mul10(mul10), .mulhu11(mulhu11), .mulh14(mulh14));
  Multiplexer #(.select(4), .width(32), .enable("false")) multiplexer_1 (
    .in0(add0), .in1(and1), .in2(or2), .in3(xor3), .in4(srl4), .in5(sra5), .in6(sll6), .in7(slt7),
    .in8(divu8), .in9(remu9), .in10(mul10), .in11(mulhu11), .in12(sub12), .in13(B), .in14(mulh14),
    .out(Result), .sel(ALUSel));  // open: in15

  // Other names for the same wires on the sheet: bsel13[31:0] = B

  // Notes on the sheet:
  //   INPUTS to your circuit
  //   DON'T CHANGE THE LOCATIONS OF THE INPUTS AND OUTPUTS!
  //   OUTPUT from your circuit
endmodule

module mul_helper (
  input  [31:0] input_1,
  input  [31:0] input_2,
  output [31:0] mul10,
  output [31:0] mulhu11,
  output [31:0] mulh14
);

  wire comparator_1_eq, result_sign;
  wire [31:0] adder_1_out, adder_2_out, adder_3_out, cmp, input_1_abs, input_2_abs, multiplexer_1_out,
       multiplier_1_out, temp, xor_1_out, xor_2_out, xor_3_out, xor_4_out, xor_6_out;

  assign xor_1_out = temp ^ {32{1'b1}};  // XOR_Gate xor_1, 32 bits wide
  assign xor_2_out = temp ^ {32{1'b1}};  // XOR_Gate xor_2, 32 bits wide
  Adder #(.width(32)) adder_1 (.a(xor_2_out), .b(32'h1), .out(adder_1_out));  // open: cin, cout
  Comparator #(.width(32)) comparator_1 (.a(cmp), .b({32{1'b0}}), .eq(comparator_1_eq));  // open: gt, lt
  assign xor_3_out = input_1 ^ {32{1'b1}};  // XOR_Gate xor_3, 32 bits wide
  assign xor_4_out = input_2 ^ {32{1'b1}};  // XOR_Gate xor_4, 32 bits wide
  Multiplexer #(.width(32), .enable("false")) multiplexer_1 (
    .in0(xor_1_out), .in1(adder_1_out), .out(multiplexer_1_out), .sel(comparator_1_eq));
  Adder #(.width(32)) adder_2 (.a(xor_3_out), .b(32'h1), .out(adder_2_out));  // open: cin, cout
  Adder #(.width(32)) adder_3 (.a(xor_4_out), .b(32'h1), .out(adder_3_out));  // open: cin, cout
  Multiplier #(.width(32)) multiplier_1 (
    .a(input_1_abs), .b(input_2_abs), .out(multiplier_1_out), .cout(temp));  // open: cin
  Multiplexer #(.width(32), .enable("false")) multiplexer_2 (
    .in0(temp), .in1(multiplexer_1_out), .out(mulh14), .sel(result_sign));
  xor xor_5 (result_sign, input_1[31], input_2[31]);
  Multiplier #(.width(32)) multiplier_2 (.a(input_1), .b(input_2), .out(mul10), .cout(mulhu11));  // open: cin
  Multiplexer #(.width(32), .enable("false")) multiplexer_3 (
    .in0(input_1), .in1(adder_2_out), .out(input_1_abs), .sel(input_1[31]));
  Multiplexer #(.width(32), .enable("false")) multiplexer_4 (
    .in0(input_2), .in1(adder_3_out), .out(input_2_abs), .sel(input_2[31]));
  assign xor_6_out = multiplier_1_out ^ {32{1'b1}};  // XOR_Gate xor_6, 32 bits wide
  Adder #(.width(32)) adder_4 (.a(xor_6_out), .b(32'h1), .out(cmp));  // open: cin, cout

  // Other names for the same wires on the sheet: input_1_sign = input_1[31]; input_2_sign = input_2[31]
endmodule
