// Logisim project control_logic.circ as structural Verilog: 1 circuit, main circuit control_logic
module control_logic (
  input  [31:0] inst,
  input  BrEq,
  input  BrLt,
  output PCSel,
  output RegWEn,
  output [2:0] ImmSel,
  output BrUn,
  output ASel,
  output BSel,
  output [3:0] ALUSel,
  output MemRW,
  output [1:0] WBSel
);

  wire ALUSel_0_0, ALUSel_0_1, ALUSel_0_2, ALUSel_0_3, ALUSel_0_4, ALUSel_0_5, ALUSel_0_6, ALUSel_0_7,
       ALUSel_0_8, ALUSel_0_9, ALUSel_0_10, ALUSel_1_0, ALUSel_1_1, ALUSel_1_2, ALUSel_1_3, ALUSel_1_4,
       ALUSel_1_5, ALUSel_1_6, ALUSel_1_7, ALUSel_1_8, ALUSel_1_9, ALUSel_1_10, ALUSel_2_0, ALUSel_2_1,
       ALUSel_2_2, ALUSel_2_3, ALUSel_2_4, ALUSel_2_5, ALUSel_2_6, ALUSel_2_7, ALUSel_2_8, ALUSel_2_9,
       ALUSel_2_10, ALUSel_3_0, ALUSel_3_1, ALUSel_3_2, ALUSel_3_3, ALUSel_3_4, ALUSel_3_5, ALUSel_3_6,
       and_1_out, and_3_out, comparator_1_eq, comparator_2_eq, comparator_3_eq, comparator_4_eq,
       comparator_5_eq, comparator_6_eq, comparator_7_eq, comparator_8_eq, comparator_9_eq, comparator_10_eq,
       comparator_11_eq, comparator_12_eq, comparator_13_eq, comparator_14_eq, comparator_15_eq,
       comparator_16_eq, comparator_17_eq, comparator_18_eq, comparator_19_eq, comparator_20_eq,
       comparator_21_eq, comparator_22_eq, comparator_23_eq, comparator_24_eq, comparator_25_eq,
       comparator_26_eq, comparator_27_eq, comparator_28_eq, comparator_29_eq, comparator_30_eq,
       comparator_31_eq, comparator_32_eq, comparator_33_eq, comparator_34_eq, comparator_35_eq,
       comparator_36_eq, comparator_37_eq, comparator_38_eq, comparator_39_eq, comparator_40_eq,
       comparator_41_eq, comparator_42_eq, comparator_43_eq, comparator_44_eq, comparator_45_eq,
       comparator_46_eq, comparator_47_eq, comparator_48_eq, comparator_49_eq, comparator_50_eq,
       comparator_51_eq, comparator_52_eq, comparator_53_eq, comparator_54_eq, comparator_55_eq,
       comparator_56_eq, comparator_57_eq, comparator_58_eq, comparator_59_eq, comparator_60_eq,
       comparator_61_eq, comparator_62_eq, comparator_63_eq, comparator_64_eq, comparator_65_eq,
       comparator_66_eq, comparator_67_eq, comparator_68_eq, comparator_69_eq, comparator_70_eq,
       comparator_71_eq, comparator_72_eq, comparator_73_eq, comparator_74_eq, comparator_75_eq,
       comparator_76_eq, comparator_77_eq, comparator_78_eq, comparator_79_eq, comparator_80_eq,
       comparator_81_eq, comparator_82_eq, comparator_83_eq, comparator_84_eq, comparator_85_eq,
       comparator_86_eq, comparator_87_eq, comparator_88_eq, comparator_89_eq, comparator_90_eq,
       comparator_91_eq, comparator_92_eq, comparator_93_eq, comparator_94_eq, comparator_95_eq,
       comparator_96_eq, comparator_97_eq, comparator_98_eq, comparator_99_eq, comparator_100_eq,
       comparator_101_eq, comparator_102_eq, comparator_103_eq, comparator_104_eq, comparator_105_eq,
       comparator_106_eq, comparator_107_eq, comparator_108_eq, comparator_109_eq, comparator_110_eq,
       comparator_111_eq, comparator_112_eq, comparator_113_eq, comparator_114_eq, comparator_115_eq,
       comparator_116_eq, comparator_117_eq, comparator_118_eq, comparator_119_eq, comparator_120_eq,
       comparator_121_eq, comparator_122_eq, comparator_123_eq, comparator_127_eq, comparator_128_eq,
       comparator_129_eq, comparator_130_eq, comparator_131_eq, comparator_132_eq, comparator_133_eq,
       comparator_134_eq, comparator_135_eq, comparator_136_eq, comparator_137_eq, comparator_138_eq,
       comparator_139_eq, comparator_140_eq, multiplexer_1_out, not_1_out, not_2_out, not_3_out, or_5_out;

  not not_1 (not_1_out, BrLt);
  not not_2 (not_2_out, BrLt);
  Comparator #(.width(7)) comparator_1 (.a({7{1'b0}}), .b(inst[31:25]), .eq(comparator_1_eq));  // open: gt, lt
  Comparator #(.width(3)) comparator_2 (.a(3'b111), .b(inst[14:12]), .eq(comparator_2_eq));  // open: gt, lt
  Comparator #(.width(7)) comparator_3 (.a(7'b0110011), .b(inst[6:0]), .eq(comparator_3_eq));  // open: gt, lt
  Comparator #(.width(7)) comparator_4 (.a({7{1'b0}}), .b(inst[31:25]), .eq(comparator_4_eq));  // open: gt, lt
  Comparator #(.width(3)) comparator_5 (.a(3'b100), .b(inst[14:12]), .eq(comparator_5_eq));  // open: gt, lt
  Comparator #(.width(7)) comparator_6 (.a(7'b0110011), .b(inst[6:0]), .eq(comparator_6_eq));  // open: gt, lt
  Comparator #(.width(7)) comparator_7 (.a(7'b0100000), .b(inst[31:25]), .eq(comparator_7_eq));  // open: gt, lt
  Comparator #(.width(3)) comparator_8 (.a(3'b101), .b(inst[14:12]), .eq(comparator_8_eq));  // open: gt, lt
  Comparator #(.width(7)) comparator_9 (.a(7'b0110011), .b(inst[6:0]), .eq(comparator_9_eq));  // open: gt, lt
  Comparator #(.width(7)) comparator_10 (.a({7{1'b0}}), .b(inst[31:25]), .eq(comparator_10_eq));  // open: gt, lt
  Comparator #(.width(3)) comparator_11 (.a(3'b010), .b(inst[14:12]), .eq(comparator_11_eq));  // open: gt, lt
  Comparator #(.width(7)) comparator_12 (.a(7'b0110011), .b(inst[6:0]), .eq(comparator_12_eq));  // open: gt, lt
  Comparator #(.width(7)) comparator_13 (.a(7'b0000001), .b(inst[31:25]), .eq(comparator_13_eq));  // open: gt, lt
  Comparator #(.width(3)) comparator_14 (.a(3'b111), .b(inst[14:12]), .eq(comparator_14_eq));  // open: gt, lt
  Comparator #(.width(7)) comparator_15 (.a(7'b0110011), .b(inst[6:0]), .eq(comparator_15_eq));  // open: gt, lt
  Comparator #(.width(7)) comparator_16 (.a(7'b0000001), .b(inst[31:25]), .eq(comparator_16_eq));  // open: gt, lt
  Comparator #(.width(3)) comparator_17 (.a(3'b011), .b(inst[14:12]), .eq(comparator_17_eq));  // open: gt, lt
  Comparator #(.width(7)) comparator_18 (.a(7'b0110011), .b(inst[6:0]), .eq(comparator_18_eq));  // open: gt, lt
  Comparator #(.width(3)) comparator_19 (.a(3'b111), .b(inst[14:12]), .eq(comparator_19_eq));  // open: gt, lt
  Comparator #(.width(7)) comparator_20 (.a(7'b0010011), .b(inst[6:0]), .eq(comparator_20_eq));  // open: gt, lt
  Comparator #(.width(3)) comparator_21 (.a(3'b100), .b(inst[14:12]), .eq(comparator_21_eq));  // open: gt, lt
  Comparator #(.width(7)) comparator_22 (.a(7'b0010011), .b(inst[6:0]), .eq(comparator_22_eq));  // open: gt, lt
  Comparator #(.width(7)) comparator_23 (.a(7'b0100000), .b(inst[31:25]), .eq(comparator_23_eq));  // open: gt, lt
  Comparator #(.width(3)) comparator_24 (.a(3'b101), .b(inst[14:12]), .eq(comparator_24_eq));  // open: gt, lt
  Comparator #(.width(7)) comparator_25 (.a(7'b0010011), .b(inst[6:0]), .eq(comparator_25_eq));  // open: gt, lt
  Comparator #(.width(3)) comparator_26 (.a(3'b010), .b(inst[14:12]), .eq(comparator_26_eq));  // open: gt, lt
  Comparator #(.width(7)) comparator_27 (.a(7'b0010011), .b(inst[6:0]), .eq(comparator_27_eq));  // open: gt, lt
  Comparator #(.width(7)) comparator_28 (.a({7{1'b0}}), .b(inst[31:25]), .eq(comparator_28_eq));  // open: gt, lt
  Comparator #(.width(3)) comparator_29 (.a(3'b101), .b(inst[14:12]), .eq(comparator_29_eq));  // open: gt, lt
  Comparator #(.width(7)) comparator_30 (.a(7'b0110011), .b(inst[6:0]), .eq(comparator_30_eq));  // open: gt, lt
  Comparator #(.width(7)) comparator_31 (.a(7'b0100000), .b(inst[31:25]), .eq(comparator_31_eq));  // open: gt, lt
  Comparator #(.width(3)) comparator_32 (.a(3'b101), .b(inst[14:12]), .eq(comparator_32_eq));  // open: gt, lt
  Comparator #(.width(7)) comparator_33 (.a(7'b0110011), .b(inst[6:0]), .eq(comparator_33_eq));  // open: gt, lt
  Comparator #(.width(7)) comparator_34 (.a({7{1'b0}}), .b(inst[31:25]), .eq(comparator_34_eq));  // open: gt, lt
  Comparator #(.width(3)) comparator_35 (.a(3'b001), .b(inst[14:12]), .eq(comparator_35_eq));  // open: gt, lt
  Comparator #(.width(7)) comparator_36 (.a(7'b0110011), .b(inst[6:0]), .eq(comparator_36_eq));  // open: gt, lt
  Comparator #(.width(7)) comparator_37 (.a({7{1'b0}}), .b(inst[31:25]), .eq(comparator_37_eq));  // open: gt, lt
  Comparator #(.width(3)) comparator_38 (.a(3'b010), .b(inst[14:12]), .eq(comparator_38_eq));  // open: gt, lt
  Comparator #(.width(7)) comparator_39 (.a(7'b0110011), .b(inst[6:0]), .eq(comparator_39_eq));  // open: gt, lt
  Comparator #(.width(7)) comparator_40 (.a(7'b0100000), .b(inst[31:25]), .eq(comparator_40_eq));  // open: gt, lt
  Comparator #(.width(3)) comparator_41 (.a(3'b000), .b(inst[14:12]), .eq(comparator_41_eq));  // open: gt, lt
  Comparator #(.width(7)) comparator_42 (.a(7'b0110011), .b(inst[6:0]), .eq(comparator_42_eq));  // open: gt, lt
  Comparator #(.width(7)) comparator_43 (.a({7{1'b0}}), .b(inst[31:25]), .eq(comparator_43_eq));  // open: gt, lt
  Comparator #(.width(3)) comparator_44 (.a(3'b101), .b(inst[14:12]), .eq(comparator_44_eq));  // open: gt, lt
  Comparator #(.width(7)) comparator_45 (.a(7'b0010011), .b(inst[6:0]), .eq(comparator_45_eq));  // open: gt, lt
  Comparator #(.width(7)) comparator_46 (.a(7'b0100000), .b(inst[31:25]), .eq(comparator_46_eq));  // open: gt, lt
  Comparator #(.width(3)) comparator_47 (.a(3'b101), .b(inst[14:12]), .eq(comparator_47_eq));  // open: gt, lt
  Comparator #(.width(7)) comparator_48 (.a(7'b0010011), .b(inst[6:0]), .eq(comparator_48_eq));  // open: gt, lt
  Comparator #(.width(3)) comparator_49 (.a(3'b010), .b(inst[14:12]), .eq(comparator_49_eq));  // open: gt, lt
  Comparator #(.width(7)) comparator_50 (.a(7'b0010011), .b(inst[6:0]), .eq(comparator_50_eq));  // open: gt, lt
  Comparator #(.width(3)) comparator_51 (.a(3'b000), .b(inst[14:12]), .eq(comparator_51_eq));  // open: gt, lt
  Comparator #(.width(7)) comparator_52 (.a(7'b1100111), .b(inst[6:0]), .eq(comparator_52_eq));  // open: gt, lt
  and and1 (ALUSel_0_0, comparator_1_eq, comparator_2_eq, comparator_3_eq);
  and xor3 (ALUSel_0_1, comparator_4_eq, comparator_5_eq, comparator_6_eq);
  and sra5 (ALUSel_0_2, comparator_7_eq, comparator_8_eq, comparator_9_eq);
  and slt7 (ALUSel_0_3, comparator_10_eq, comparator_11_eq, comparator_12_eq);
  and remu9 (ALUSel_0_4, comparator_13_eq, comparator_14_eq, comparator_15_eq);
  and mulhu11 (ALUSel_0_5, comparator_16_eq, comparator_17_eq, comparator_18_eq);
  and andi1 (ALUSel_0_6, comparator_19_eq, comparator_20_eq);
  and xori3 (ALUSel_0_7, comparator_21_eq, comparator_22_eq);
  and srai5 (ALUSel_0_8, comparator_23_eq, comparator_24_eq, comparator_25_eq);
  and slti7 (ALUSel_0_9, comparator_26_eq, comparator_27_eq);
  and srl4 (ALUSel_2_0, comparator_28_eq, comparator_29_eq, comparator_30_eq);
  and sra5_2 (ALUSel_2_1, comparator_31_eq, comparator_32_eq, comparator_33_eq);
  and sll6_2 (ALUSel_2_2, comparator_34_eq, comparator_35_eq, comparator_36_eq);
  and slt7_3 (ALUSel_2_3, comparator_37_eq, comparator_38_eq, comparator_39_eq);
  and sub12 (ALUSel_2_4, comparator_40_eq, comparator_41_eq, comparator_42_eq);
  and srli4 (ALUSel_2_5, comparator_43_eq, comparator_44_eq, comparator_45_eq);
  and srai5_2 (ALUSel_2_6, comparator_46_eq, comparator_47_eq, comparator_48_eq);
  and slti7_3 (ALUSel_2_7, comparator_49_eq, comparator_50_eq);
  or or_1 (ALUSel[2], ALUSel_2_8, ALUSel_2_0, ALUSel_2_1, ALUSel_2_2, ALUSel_2_3, ALUSel_2_10, ALUSel_2_4, ALUSel_2_5, ALUSel_2_6, ALUSel_2_7, ALUSel_2_9);
  Comparator #(.width(3)) comparator_53 (.a(3'b010), .b(inst[14:12]), .eq(comparator_53_eq));  // open: gt, lt
  Comparator #(.width(7)) comparator_54 (.a(7'b0100011), .b(inst[6:0]), .eq(comparator_54_eq));  // open: gt, lt
  Comparator #(.width(7)) comparator_55 (.a(7'b1101111), .b(inst[6:0]), .eq(comparator_55_eq));  // open: gt, lt
  and and_1 (and_1_out, comparator_51_eq, comparator_52_eq);
  Comparator #(.width(7)) comparator_56 (.a(7'b0110011), .b(inst[6:0]), .eq(comparator_56_eq));  // open: gt, lt
  Comparator #(.width(7)) comparator_57 (.a(7'b0010011), .b(inst[6:0]), .eq(comparator_57_eq));  // open: gt, lt
  Comparator #(.width(7)) comparator_58 (.a(7'b0010111), .b(inst[6:0]), .eq(comparator_58_eq));  // open: gt, lt
  Comparator #(.width(7)) comparator_59 (.a(7'b0110111), .b(inst[6:0]), .eq(comparator_59_eq));  // open: gt, lt
  not not_3 (not_3_out, BrEq);
  or or_2 (ALUSel[0], ALUSel_0_0, ALUSel_0_1, ALUSel_0_2, ALUSel_0_3, ALUSel_0_4, ALUSel_0_10, ALUSel_0_5, ALUSel_0_6, ALUSel_0_7, ALUSel_0_8, ALUSel_0_9);
  and and_2 (MemRW, comparator_53_eq, comparator_54_eq);
  or or_3 (WBSel[1], comparator_55_eq, and_1_out);
  or or_4 (WBSel[0], comparator_56_eq, comparator_57_eq, comparator_58_eq, comparator_59_eq);
  Comparator #(.width(7)) comparator_60 (.a(7'b1100011), .b(inst[6:0]), .eq(comparator_60_eq));  // open: gt, lt
  Multiplexer #(.select(3), .enable("false")) multiplexer_1 (
    .in0(BrEq), .in1(not_3_out), .in4(BrLt), .in5(not_2_out), .in6(BrLt), .in7(not_1_out),
    .out(multiplexer_1_out), .sel(inst[14:12]));  // open: in2, in3
  Comparator #(.width(7)) comparator_61 (.a(7'b0000011), .b(inst[6:0]), .eq(comparator_61_eq));  // open: gt, lt
  Comparator #(.width(7)) comparator_62 (.a(7'b0010011), .b(inst[6:0]), .eq(comparator_62_eq));  // open: gt, lt
  Comparator #(.width(7)) comparator_63 (.a(7'b0110011), .b(inst[6:0]), .eq(comparator_63_eq));  // open: gt, lt
  Comparator #(.width(7)) comparator_64 (.a(7'b0010111), .b(inst[6:0]), .eq(comparator_64_eq));  // open: gt, lt
  Comparator #(.width(7)) comparator_65 (.a(7'b0110111), .b(inst[6:0]), .eq(comparator_65_eq));  // open: gt, lt
  Comparator #(.width(7)) comparator_66 (.a(7'b1101111), .b(inst[6:0]), .eq(comparator_66_eq));  // open: gt, lt
  Comparator #(.width(7)) comparator_67 (.a(7'b1100111), .b(inst[6:0]), .eq(comparator_67_eq));  // open: gt, lt
  Comparator #(.width(7)) comparator_68 (.a(7'b1100011), .b(inst[6:0]), .eq(comparator_68_eq));  // open: gt, lt
  Comparator #(.width(3)) comparator_69 (.a(3'b110), .b(inst[14:12]), .eq(comparator_69_eq));  // open: gt, lt
  Comparator #(.width(3)) comparator_70 (.a(3'b111), .b(inst[14:12]), .eq(comparator_70_eq));  // open: gt, lt
  Comparator #(.width(7)) comparator_71 (.a(7'b1100011), .b(inst[6:0]), .eq(comparator_71_eq));  // open: gt, lt
  Comparator #(.width(7)) comparator_72 (.a(7'b0010111), .b(inst[6:0]), .eq(comparator_72_eq));  // open: gt, lt
  Comparator #(.width(7)) comparator_73 (.a(7'b1101111), .b(inst[6:0]), .eq(comparator_73_eq));  // open: gt, lt
  Comparator #(.width(7)) comparator_74 (.a(7'b0010011), .b(inst[6:0]), .eq(comparator_74_eq));  // open: gt, lt
  Comparator #(.width(7)) comparator_75 (.a(7'b0100011), .b(inst[6:0]), .eq(comparator_75_eq));  // open: gt, lt
  Comparator #(.width(7)) comparator_76 (.a(7'b0000011), .b(inst[6:0]), .eq(comparator_76_eq));  // open: gt, lt
  Comparator #(.width(7)) comparator_77 (.a(7'b1100011), .b(inst[6:0]), .eq(comparator_77_eq));  // open: gt, lt
  Comparator #(.width(7)) comparator_78 (.a(7'b0110111), .b(inst[6:0]), .eq(comparator_78_eq));  // open: gt, lt
  Comparator #(.width(7)) comparator_79 (.a(7'b0010111), .b(inst[6:0]), .eq(comparator_79_eq));  // open: gt, lt
  Comparator #(.width(7)) comparator_80 (.a(7'b1101111), .b(inst[6:0]), .eq(comparator_80_eq));  // open: gt, lt
  Comparator #(.width(7)) comparator_81 (.a(7'b1100111), .b(inst[6:0]), .eq(comparator_81_eq));  // open: gt, lt
  Comparator #(.width(7)) comparator_82 (.a({7{1'b0}}), .b(inst[31:25]), .eq(comparator_82_eq));  // open: gt, lt
  Comparator #(.width(3)) comparator_83 (.a(3'b110), .b(inst[14:12]), .eq(comparator_83_eq));  // open: gt, lt
  Comparator #(.width(7)) comparator_84 (.a(7'b0110011), .b(inst[6:0]), .eq(comparator_84_eq));  // open: gt, lt
  Comparator #(.width(7)) comparator_85 (.a({7{1'b0}}), .b(inst[31:25]), .eq(comparator_85_eq));  // open: gt, lt
  Comparator #(.width(3)) comparator_86 (.a(3'b100), .b(inst[14:12]), .eq(comparator_86_eq));  // open: gt, lt
  Comparator #(.width(7)) comparator_87 (.a(7'b0110011), .b(inst[6:0]), .eq(comparator_87_eq));  // open: gt, lt
  Comparator #(.width(7)) comparator_88 (.a({7{1'b0}}), .b(inst[31:25]), .eq(comparator_88_eq));  // open: gt, lt
  Comparator #(.width(3)) comparator_89 (.a(3'b001), .b(inst[14:12]), .eq(comparator_89_eq));  // open: gt, lt
  Comparator #(.width(7)) comparator_90 (.a(7'b0110011), .b(inst[6:0]), .eq(comparator_90_eq));  // open: gt, lt
  Comparator #(.width(7)) comparator_91 (.a({7{1'b0}}), .b(inst[31:25]), .eq(comparator_91_eq));  // open: gt, lt
  Comparator #(.width(3)) comparator_92 (.a(3'b010), .b(inst[14:12]), .eq(comparator_92_eq));  // open: gt, lt
  Comparator #(.width(7)) comparator_93 (.a(7'b0110011), .b(inst[6:0]), .eq(comparator_93_eq));  // open: gt, lt
  Comparator #(.width(7)) comparator_94 (.a(7'b0000001), .b(inst[31:25]), .eq(comparator_94_eq));  // open: gt, lt
  Comparator #(.width(3)) comparator_95 (.a(3'b000), .b(inst[14:12]), .eq(comparator_95_eq));  // open: gt, lt
  Comparator #(.width(7)) comparator_96 (.a(7'b0110011), .b(inst[6:0]), .eq(comparator_96_eq));  // open: gt, lt
  Comparator #(.width(7)) comparator_97 (.a(7'b0000001), .b(inst[31:25]), .eq(comparator_97_eq));  // open: gt, lt
  Comparator #(.width(3)) comparator_98 (.a(3'b011), .b(inst[14:12]), .eq(comparator_98_eq));  // open: gt, lt
  Comparator #(.width(7)) comparator_99 (.a(7'b0110011), .b(inst[6:0]), .eq(comparator_99_eq));  // open: gt, lt
  Comparator #(.width(3)) comparator_100 (.a(3'b100), .b(inst[14:12]), .eq(comparator_100_eq));  // open: gt, lt
  Comparator #(.width(7)) comparator_101 (.a(7'b0010011), .b(inst[6:0]), .eq(comparator_101_eq));  // open: gt, lt
  Comparator #(.width(7)) comparator_102 (.a({7{1'b0}}), .b(inst[31:25]), .eq(comparator_102_eq));  // open: gt, lt
  Comparator #(.width(3)) comparator_103 (.a(3'b001), .b(inst[14:12]), .eq(comparator_103_eq));  // open: gt, lt
  Comparator #(.width(7)) comparator_104 (.a(7'b0010011), .b(inst[6:0]), .eq(comparator_104_eq));  // open: gt, lt
  Comparator #(.width(3)) comparator_105 (.a(3'b010), .b(inst[14:12]), .eq(comparator_105_eq));  // open: gt, lt
  Comparator #(.width(7)) comparator_106 (.a(7'b0010011), .b(inst[6:0]), .eq(comparator_106_eq));  // open: gt, lt
  Comparator #(.width(7)) comparator_107 (.a(7'b0100000), .b(inst[31:25]), .eq(comparator_107_eq));  // open: gt, lt
  Comparator #(.width(3)) comparator_108 (.a(3'b000), .b(inst[14:12]), .eq(comparator_108_eq));  // open: gt, lt
  Comparator #(.width(7)) comparator_109 (.a(7'b0110011), .b(inst[6:0]), .eq(comparator_109_eq));  // open: gt, lt
  and and_3 (and_3_out, comparator_60_eq, multiplexer_1_out);
  Comparator #(.width(7)) comparator_110 (.a(7'b1100111), .b(inst[6:0]), .eq(comparator_110_eq));  // open: gt, lt
  Comparator #(.width(7)) comparator_111 (.a(7'b1101111), .b(inst[6:0]), .eq(comparator_111_eq));  // open: gt, lt
  Multiplexer #(.select(5), .width(3), .enable("false")) multiplexer_2 (
    .in0(3'b000), .in4(3'b000), .in5(3'b001), .in8(3'b010), .in12(3'b011), .in13(3'b001), .in24(3'b100),
    .in25(3'b000), .in27(3'b101), .out(ImmSel), .sel(inst[6:2]));  // open: in1, in2, in3, in6, in7, in9, in10, in11, in14, in15, in16, in17, in18, in19, in20, in21, in22, in23, in26, in28, in29, in30, in31
  or or_5 (or_5_out, comparator_69_eq, comparator_70_eq);
  Comparator #(.width(7)) comparator_112 (.a(7'b0000001), .b(inst[31:25]), .eq(comparator_112_eq));  // open: gt, lt
  Comparator #(.width(3)) comparator_113 (.a(3'b101), .b(inst[14:12]), .eq(comparator_113_eq));  // open: gt, lt
  Comparator #(.width(7)) comparator_114 (.a(7'b0110011), .b(inst[6:0]), .eq(comparator_114_eq));  // open: gt, lt
  Comparator #(.width(7)) comparator_115 (.a(7'b0000001), .b(inst[31:25]), .eq(comparator_115_eq));  // open: gt, lt
  Comparator #(.width(3)) comparator_116 (.a(3'b111), .b(inst[14:12]), .eq(comparator_116_eq));  // open: gt, lt
  Comparator #(.width(7)) comparator_117 (.a(7'b0110011), .b(inst[6:0]), .eq(comparator_117_eq));  // open: gt, lt
  Comparator #(.width(7)) comparator_118 (.a(7'b0000001), .b(inst[31:25]), .eq(comparator_118_eq));  // open: gt, lt
  Comparator #(.width(3)) comparator_119 (.a(3'b000), .b(inst[14:12]), .eq(comparator_119_eq));  // open: gt, lt
  Comparator #(.width(7)) comparator_120 (.a(7'b0110011), .b(inst[6:0]), .eq(comparator_120_eq));  // open: gt, lt
  Comparator #(.width(7)) comparator_121 (.a(7'b0000001), .b(inst[31:25]), .eq(comparator_121_eq));  // open: gt, lt
  Comparator #(.width(3)) comparator_122 (.a(3'b011), .b(inst[14:12]), .eq(comparator_122_eq));  // open: gt, lt
  Comparator #(.width(7)) comparator_123 (.a(7'b0110011), .b(inst[6:0]), .eq(comparator_123_eq));  // open: gt, lt
  Comparator #(.width(7)) comparator_124 (.a(7'b0110111), .b(inst[6:0]), .eq(ALUSel_0_10));  // open: gt, lt
  Comparator #(.width(7)) comparator_125 (.a(7'b0110111), .b(inst[6:0]), .eq(ALUSel_2_8));  // open: gt, lt
  Comparator #(.width(7)) comparator_126 (.a(7'b0110111), .b(inst[6:0]), .eq(ALUSel_3_5));  // open: gt, lt
  or or_6 (PCSel, and_3_out, comparator_110_eq, comparator_111_eq);
  or or_7 (RegWEn, comparator_61_eq, comparator_62_eq, comparator_63_eq, comparator_64_eq, comparator_65_eq, comparator_66_eq, comparator_67_eq);
  and and_4 (BrUn, comparator_68_eq, or_5_out);
  or or_8 (ASel, comparator_71_eq, comparator_72_eq, comparator_73_eq);
  or or_9 (BSel, comparator_74_eq, comparator_75_eq, comparator_76_eq, comparator_77_eq, comparator_78_eq, comparator_79_eq, comparator_80_eq, comparator_81_eq);
  and or2 (ALUSel_1_0, comparator_82_eq, comparator_83_eq, comparator_84_eq);
  and xor3_2 (ALUSel_1_1, comparator_85_eq, comparator_86_eq, comparator_87_eq);
  and sll6 (ALUSel_1_2, comparator_88_eq, comparator_89_eq, comparator_90_eq);
  and slt7_2 (ALUSel_1_3, comparator_91_eq, comparator_92_eq, comparator_93_eq);
  and mul10 (ALUSel_1_4, comparator_94_eq, comparator_95_eq, comparator_96_eq);
  and mulhu11_2 (ALUSel_1_5, comparator_97_eq, comparator_98_eq, comparator_99_eq);
  and xori3_2 (ALUSel_1_6, comparator_100_eq, comparator_101_eq);
  and slli6 (ALUSel_1_7, comparator_102_eq, comparator_103_eq, comparator_104_eq);
  and slti9_2 (ALUSel_1_8, comparator_105_eq, comparator_106_eq);
  and divu8 (ALUSel_3_0, comparator_112_eq, comparator_113_eq, comparator_114_eq);
  and remu9_2 (ALUSel_3_1, comparator_115_eq, comparator_116_eq, comparator_117_eq);
  and mul10_2 (ALUSel_3_2, comparator_118_eq, comparator_119_eq, comparator_120_eq);
  and mulhu11_3 (ALUSel_3_3, comparator_121_eq, comparator_122_eq, comparator_123_eq);
  and sub12_2 (ALUSel_3_4, comparator_107_eq, comparator_108_eq, comparator_109_eq);
  Comparator #(.width(7)) comparator_127 (.a({7{1'b0}}), .b(inst[31:25]), .eq(comparator_127_eq));  // open: gt, lt
  Comparator #(.width(3)) comparator_128 (.a(3'b001), .b(inst[14:12]), .eq(comparator_128_eq));  // open: gt, lt
  Comparator #(.width(7)) comparator_129 (.a(7'b0010011), .b(inst[6:0]), .eq(comparator_129_eq));  // open: gt, lt
  or or_10 (ALUSel[1], ALUSel_1_4, ALUSel_1_0, ALUSel_1_1, ALUSel_1_2, ALUSel_1_3, ALUSel_1_10, ALUSel_1_5, ALUSel_1_6, ALUSel_1_7, ALUSel_1_8, ALUSel_1_9);
  or or_11 (ALUSel[3], ALUSel_3_2, ALUSel_3_0, ALUSel_3_1, ALUSel_3_6, ALUSel_3_3, ALUSel_3_4, ALUSel_3_5);
  and and_5 (ALUSel_2_9, comparator_127_eq, comparator_128_eq, comparator_129_eq);
  Comparator #(.width(3)) comparator_130 (.a(3'b110), .b(inst[14:12]), .eq(comparator_130_eq));  // open: gt, lt
  Comparator #(.width(7)) comparator_131 (.a(7'b0010011), .b(inst[6:0]), .eq(comparator_131_eq));  // open: gt, lt
  Comparator #(.width(7)) comparator_132 (.a(7'b0000001), .b(inst[31:25]), .eq(comparator_132_eq));  // open: gt, lt
  Comparator #(.width(3)) comparator_133 (.a(3'b001), .b(inst[14:12]), .eq(comparator_133_eq));  // open: gt, lt
  Comparator #(.width(7)) comparator_134 (.a(7'b0110011), .b(inst[6:0]), .eq(comparator_134_eq));  // open: gt, lt
  Comparator #(.width(7)) comparator_135 (.a(7'b0000001), .b(inst[31:25]), .eq(comparator_135_eq));  // open: gt, lt
  Comparator #(.width(3)) comparator_136 (.a(3'b001), .b(inst[14:12]), .eq(comparator_136_eq));  // open: gt, lt
  Comparator #(.width(7)) comparator_137 (.a(7'b0110011), .b(inst[6:0]), .eq(comparator_137_eq));  // open: gt, lt
  Comparator #(.width(7)) comparator_138 (.a(7'b0000001), .b(inst[31:25]), .eq(comparator_138_eq));  // open: gt, lt
  Comparator #(.width(3)) comparator_139 (.a(3'b001), .b(inst[14:12]), .eq(comparator_139_eq));  // open: gt, lt
  Comparator #(.width(7)) comparator_140 (.a(7'b0110011), .b(inst[6:0]), .eq(comparator_140_eq));  // open: gt, lt
  and ori6 (ALUSel_1_10, comparator_130_eq, comparator_131_eq);
  and mulh14 (ALUSel_1_9, comparator_132_eq, comparator_133_eq, comparator_134_eq);
  and mulh14_2 (ALUSel_2_10, comparator_135_eq, comparator_136_eq, comparator_137_eq);
  and mulh14_3 (ALUSel_3_6, comparator_138_eq, comparator_139_eq, comparator_140_eq);

  // Other names for the same wires on the sheet: ALUSel_0 = ALUSel[0]; ALUSel_1 = ALUSel[1]; ALUSel_2 = ALUSel[2];
  //   ALUSel_3 = ALUSel[3]; Opcode[6:0] = inst[6:0]; Opcode_5[4:0] = inst[6:2]; fun3[2:0] = inst[14:12];
  //   fun7[6:0] = inst[31:25]; WBSel_0 = WBSel[0]; WBSel_1 = WBSel[1]

  // Notes on the sheet:
  //   INPUTS to your circuit
  //   DON'T CHANGE THE LOCATIONS OF THE INPUTS AND OUTPUTS!
  //   OUTPUT from your circuit
endmodule
