// Logisim project cpu.circ as structural Verilog: 2 circuits, main circuit main
module main (
  input  [31:0] INSTRUCTION,
  input  CLOCK,
  output [31:0] PROGRAM_COUNTER,
  output [31:0] ra,
  output [31:0] sp,
  output [31:0] t0,
  output [31:0] t1,
  output [31:0] t2,
  output [31:0] s0,
  output [31:0] s1,
  output [31:0] a0
);

  wire ASel, branch_comp_1_breq, branch_comp_1_brlt, BrUn, BSel, MemRW, or_1_out, PCSel, RegWEn, SwltSel;
  wire [1:0] WBSel;
  wire [2:0] ImmSel;
  wire [3:0] ALUSel;
  wire [4:0] rd_index, rs1_index, rs2_index;
  wire [31:0] adder_1_out, adder_2_out, ALU_output, DMEM_output, IF1_q, imm, imm_gen_1_imm,
       multiplexer_1_out, multiplexer_2_out, multiplexer_4_out, multiplexer_5_out, PROGRAM_COUNTER_1,
       rs1_value, rs2_value, Write_Data;

  control_logic control_logic_1 (
    .BSel(BSel), .BrUn(BrUn), .RegWEn(RegWEn), .ImmSel(ImmSel), .ASel(ASel), .PCSel(PCSel),
    .BrLt(branch_comp_1_brlt), .BrEq(branch_comp_1_breq),
    .inst({IF1_q[31:25], rs2_index, rs1_index, IF1_q[14:12], rd_index, IF1_q[6:0]}), .ALUSel(ALUSel),
    .MemRW(MemRW), .WBSel(WBSel));
  Adder #(.width(32)) adder_1 (.a(PROGRAM_COUNTER), .b(32'h4), .out(adder_1_out));  // open: cin, cout
  Multiplexer #(.width(32), .enable("false")) multiplexer_1 (
    .in0(adder_1_out), .in1(ALU_output), .out(multiplexer_1_out), .sel(PCSel));
  Register #(.width(32)) IF1 (
    .D(multiplexer_2_out), .clk(CLOCK),
    .Q({IF1_q[31:25], rs2_index, rs1_index, IF1_q[14:12], rd_index, IF1_q[6:0]}));  // open: en, clr
  Multiplexer #(.width(32), .enable("false")) multiplexer_2 (
    .in0(INSTRUCTION), .in1(32'h13), .out(multiplexer_2_out), .sel(PCSel));
  Register #(.width(32)) PC (.D(multiplexer_1_out), .clk(CLOCK), .Q(PROGRAM_COUNTER));  // open: en, clr
  Register #(.width(32)) register_1 (.D(PROGRAM_COUNTER), .clk(CLOCK), .Q(PROGRAM_COUNTER_1));  // open: en, clr
  imm_gen imm_gen_1 (
    .ImmSel(ImmSel), .imm(imm_gen_1_imm),
    .inst({IF1_q[31:25], rs2_index, rs1_index, IF1_q[14:12], rd_index, IF1_q[6:0]}));
  Multiplexer #(.width(32), .enable("false")) multiplexer_3 (
    .in0(imm_gen_1_imm), .in1({32{1'b0}}), .out(imm), .sel(SwltSel));
  Swlt_Comp swlt_comp_1 (
    .rs2_value(rs2_value), .S_imm(imm_gen_1_imm),
    .inst({IF1_q[31:25], rs2_index, rs1_index, IF1_q[14:12], rd_index, IF1_q[6:0]}), .Comp_Res(SwltSel));
  branch_comp branch_comp_1 (
    .BrEq(branch_comp_1_breq), .BrUn(BrUn), .rs1(rs1_value), .BrLt(branch_comp_1_brlt), .rs2(rs2_value));
  regfile_main RegFile (
    .rs2(rs2_index), .rd(rd_index), .Read_Data_1(rs1_value), .Read_Data_2(rs2_value), .ra(ra), .sp(sp),
    .t0(t0), .t1(t1), .t2(t2), .s0(s0), .s1(s1), .a0(a0), .rs1(rs1_index), .Write_Data(Write_Data),
    .RegWEn(RegWEn), .clk(CLOCK));
  Multiplexer #(.width(32), .enable("false")) multiplexer_4 (
    .in0(rs1_value), .in1(PROGRAM_COUNTER_1), .out(multiplexer_4_out), .sel(ASel));
  Multiplexer #(.width(32), .enable("false")) multiplexer_5 (
    .in0(rs2_value), .in1(imm), .out(multiplexer_5_out), .sel(BSel));
  alu Arithmetic_Logic_Unit (.Result(ALU_output), .ALUSel(ALUSel), .A(multiplexer_4_out), .B(multiplexer_5_out));
  or or_1 (or_1_out, SwltSel, MemRW);
  // mem_main DMEM: pin names not known; wires that end beside it: ALU_output, rs2_value, CLOCK, or_1_out, DMEM_output
  Adder #(.width(32)) adder_2 (.a(PROGRAM_COUNTER_1), .b(32'h4), .out(adder_2_out));  // open: cin, cout
  Multiplexer #(.select(2), .width(32), .enable("false")) multiplexer_6 (
    .in0(DMEM_output), .in1(ALU_output), .in2(adder_2_out), .out(Write_Data), .sel(WBSel));  // open: in3

  // Other names for the same wires on the sheet: clk = CLOCK

  // Notes on the sheet:
  //   Output
  //   IMEM (do **NOT** move this)
  //   Inputs
  //   It is OK to move the PC, RegFile, ALU, MEM, Branch Comp, Imm Gen, and Control Logic to wherever is most convenient for you when constructing your CPU, and to delete this text
  //   Inputs/Outputs for testing. Do **NOT** move these.
endmodule

module Swlt_Comp (
  input  [31:0] rs2_value,
  input  [31:0] S_imm,
  input  [31:0] inst,
  output Comp_Res
);

  wire and_1_out, and_4_out, comparator_1_eq, comparator_2_eq, comparator_3_lt, comparator_4_eq,
       comparator_5_eq, comparator_5_lt, comparator_7_eq, comparator_8_eq, comparator_8_lt;

  Comparator #(.width(3)) comparator_1 (.a(3'b111), .b(inst[14:12]), .eq(comparator_1_eq));  // open: gt, lt
  Comparator #(.width(7)) comparator_2 (.a(7'b0100011), .b(inst[6:0]), .eq(comparator_2_eq));  // open: gt, lt
  Comparator #(.width(32)) comparator_3 (.a(rs2_value), .b(S_imm), .lt(comparator_3_lt));  // open: gt, eq
  and and_1 (and_1_out, comparator_1_eq, comparator_2_eq);
  Comparator #(.width(3)) comparator_4 (.a(3'b111), .b(inst[14:12]), .eq(comparator_4_eq));  // open: gt, lt
  Comparator #(.width(3)) comparator_5 (
    .a(3'b111), .b(inst[14:12]), .gt(comparator_4_eq), .eq(comparator_5_eq), .lt(comparator_5_lt));
  Comparator #(.width(3)) comparator_6 (
    .a(3'b111), .b(inst[14:12]), .gt(comparator_4_eq), .eq(comparator_5_eq), .lt(comparator_5_lt));
  Comparator #(.width(7)) comparator_7 (.a(7'b0100011), .b(inst[6:0]), .eq(comparator_7_eq));  // open: gt, lt
  Comparator #(.width(7)) comparator_8 (
    .a(7'b0100011), .b(inst[6:0]), .gt(comparator_7_eq), .eq(comparator_8_eq), .lt(comparator_8_lt));
  Comparator #(.width(7)) comparator_9 (
    .a(7'b0100011), .b(inst[6:0]), .gt(comparator_7_eq), .eq(comparator_8_eq), .lt(comparator_8_lt));
  and and_2 (Comp_Res, and_1_out, comparator_3_lt);
  // AND_Gate and_3 has open pins: in0=comparator_4_eq, in1=comparator_7_eq, out=open
  and and_4 (and_4_out, comparator_5_eq, comparator_8_eq);
  and and_5 (and_4_out, comparator_5_eq, comparator_8_eq);

  // Other names for the same wires on the sheet: Opcode[6:0] = inst[6:0]; fun3[2:0] = inst[14:12]
endmodule
