// Logisim project imm_gen.circ as structural Verilog: 1 circuit, main circuit imm_gen
module imm_gen (
  input  [31:0] inst,
  input  [2:0] ImmSel,
  output [31:0] imm
);

  wire [31:0] I_imm, S_imm, SB_imm, SWLT_imm, UJ_imm;

  assign I_imm = {{20{inst[31]}}, inst[31:20]};  // Bit_Extender bit_extender_1
  assign S_imm = {{20{inst[31]}}, {inst[31:25], inst[11:7]}};  // Bit_Extender bit_extender_2
  assign SB_imm = {{19{inst[31]}}, {inst[31], inst[7], inst[30:25], inst[11:8], 1'b0}};  // Bit_Extender bit_extender_3
  assign UJ_imm = {{11{inst[31]}}, {inst[31], inst[19:12], inst[20], inst[30:21], 1'b0}};  // Bit_Extender bit_extender_4
  Multiplexer #(.select(3), .width(32), .enable("false")) multiplexer_1 (
    .in0(I_imm), .in1({inst[31:12], {12{1'b0}}}), .in2(S_imm), .in4(SB_imm), .in5(UJ_imm), .in7(SWLT_imm),
    .out(imm), .sel(ImmSel));  // open: in3, in6

  // Other names for the same wires on the sheet: U_imm[31:12] = inst[31:12]

  // Notes on the sheet:
  //   INPUTS to your circuit
  //   DON'T CHANGE THE LOCATIONS OF THE INPUTS AND OUTPUTS!
  //   OUTPUT from your circuit
endmodule
